// Logisim project B23EE1006_ALUControlUnit.circ as structural Verilog: 1 circuit, main circuit main
module main (
  input  [1:0] in_1,
  input  [5:0] in_2,
  output [3:0] out_3
);

  wire and_1_out, not_1_out, not_2_out, or_1_out;

  or or_1 (or_1_out, in_2[0], in_2[3]);
  not not_1 (not_1_out, in_1[1]);
  or or_2 (out_3[1], not_1_out, not_2_out);
  not not_2 (not_2_out, in_2[2]);
  and and_1 (and_1_out, in_1[1], in_2[1]);
  and and_2 (out_3[0], in_1[1], or_1_out);
  or or_3 (out_3[2], in_1[0], and_1_out);

  assign out_3[3] = 1'b0;

  // Notes on the sheet:
  //   (From Main Control Unit)
  //   ALUop
  //   (From Instruction Set)
  //   Function
  //   ALUControl
  //    Control Unit ALU
endmodule
