// Logisim project B23EE1006_ControlUnit.circ as structural Verilog: 2 circuits, main circuit main
module main (
  input  [5:0] Opcode,
  output [1:0] ALUOp,
  output RegDst,
  output ALUSrc,
  output MemToReg,
  output RegWrite,
  output MemRead,
  output MemWrite,
  output Branch
);

  wire For_addi_out_7, not_1_out, not_2_out, not_3_out, not_4_out, not_5_out, not_6_out, not_7_out,
       not_8_out, not_9_out, not_10_out;

  not not_1 (not_1_out, Opcode[3]);
  not not_2 (not_2_out, Opcode[3]);
  not not_3 (not_3_out, Opcode[5]);
  not not_4 (not_4_out, Opcode[1]);
  not not_5 (not_5_out, Opcode[0]);
  not not_6 (not_6_out, Opcode[5]);
  not not_7 (not_7_out, Opcode[3]);
  not not_8 (not_8_out, Opcode[1]);
  not not_9 (not_9_out, Opcode[0]);
  not not_10 (not_10_out, Opcode[2]);
  InvertAnd For_R_type (
    .in_1(Opcode[5]), .in_2(Opcode[4]), .in_3(Opcode[3]), .in_4(Opcode[2]), .in_5(Opcode[1]),
    .in_6(Opcode[0]), .out_7(ALUOp[1]));
  InvertAnd For_lw (
    .in_1(not_3_out), .in_2(Opcode[4]), .in_3(Opcode[3]), .in_4(Opcode[2]), .in_5(not_4_out),
    .in_6(not_5_out), .out_7(MemRead));
  InvertAnd For_sw (
    .in_1(not_6_out), .in_2(Opcode[4]), .in_3(not_7_out), .in_4(Opcode[2]), .in_5(not_8_out),
    .in_6(not_9_out), .out_7(MemWrite));
  InvertAnd For_beq (
    .in_1(Opcode[5]), .in_2(Opcode[4]), .in_3(Opcode[3]), .in_4(not_10_out), .in_5(Opcode[1]),
    .in_6(Opcode[0]), .out_7(ALUOp[0]));
  InvertAnd For_addi (
    .in_1(Opcode[5]), .in_2(Opcode[4]), .in_3(not_1_out), .in_4(Opcode[2]), .in_5(Opcode[1]),
    .in_6(Opcode[0]), .out_7(For_addi_out_7));
  InvertAnd For_subi (
    .in_1(Opcode[5]), .in_2(Opcode[4]), .in_3(not_2_out), .in_4(Opcode[2]), .in_5(Opcode[1]),
    .in_6(Opcode[0]), .out_7(For_addi_out_7));
  or or_1 (ALUSrc, MemRead, For_addi_out_7, MemWrite);
  or or_2 (RegWrite, ALUOp[1], For_addi_out_7, MemRead);

  assign Branch = ALUOp[0];
  assign MemToReg = MemRead;
  assign RegDst = ALUOp[1];

  // Notes on the sheet:
  //   Main Control Unit
endmodule

module InvertAnd (
  input  in_1,
  input  in_2,
  input  in_3,
  input  in_4,
  input  in_5,
  input  in_6,
  output out_7
);

  wire not_1_out, not_2_out, not_3_out, not_4_out, not_5_out, not_6_out;

  not not_1 (not_1_out, in_5);
  not not_2 (not_2_out, in_6);
  not not_3 (not_3_out, in_3);
  not not_4 (not_4_out, in_4);
  not not_5 (not_5_out, in_1);
  not not_6 (not_6_out, in_2);
  and and_1 (out_7, not_5_out, not_6_out, not_3_out, not_4_out, not_1_out, not_2_out);
endmodule
