// Logisim project B23EE1006_MAIN.circ as structural Verilog: 1 circuit, main circuit main
module main (
  input  [31:0] in_1,
  output [31:0] out_2
);

  wire and_1_out, Clock_out, main_2_alusrc, main_2_branch, main_2_regdst, main_2_regwrite, main_5_zero;
  wire [1:0] main_2_aluop;
  wire [3:0] main_4_out_3;
  wire [4:0] im0_q_3, multiplexer_1_out;
  wire [5:0] im0_q_4;
  wire [15:0] im0_q;
  wire [20:16] im0_q_2;
  wire [31:0] bit_extender_1_out, im1_q, main_1_out_5, main_3_out_7, main_3_out_8, main_6_out_5,
       multiplexer_2_out, multiplexer_3_out, shifter_1_out, undriven;

  Clock Clock (.out(Clock_out));
  Register #(.width(32)) im1 (.D(multiplexer_3_out), .Q(im1_q), .clk(Clock_out));  // open: en, clr
  Register #(.width(32)) im0 (.D(undriven), .Q({im0_q_4, im0_q_3, im0_q_2, im0_q}), .clk(Clock_out));  // open: en, clr
  B23EE1006_ALUMain_main main_1 (
    .in_1(im1_q), .in_2(32'h4), .in_3(4'b0010), .out_5(main_1_out_5));  // open: Zero, out_6, out_7
  Multiplexer #(.width(5), .enable("false")) multiplexer_1 (
    .in0(im0_q_2), .in1(im0_q[15:11]), .out(multiplexer_1_out), .sel(main_2_regdst));
  assign bit_extender_1_out = {{16{im0_q[15]}}, im0_q};  // Bit_Extender bit_extender_1
  B23EE1006_ControlUnit_main main_2 (
    .Opcode(im0_q_4), .RegDst(main_2_regdst), .ALUSrc(main_2_alusrc), .RegWrite(main_2_regwrite),
    .Branch(main_2_branch), .ALUOp(main_2_aluop));  // open: MemToReg, MemRead, MemWrite
  B23EE1006_RegisterFile_main main_3 (
    .in_2(multiplexer_1_out), .out_7(main_3_out_7), .in_1(im0_q_3), .out_8(main_3_out_8), .in_3(im0_q_2),
    .in_5(main_2_regwrite), .Clock(Clock_out), .in_4(out_2));
  Multiplexer #(.width(32), .enable("false")) multiplexer_2 (
    .in0(main_3_out_8), .in1(bit_extender_1_out), .out(multiplexer_2_out), .sel(main_2_alusrc));
  B23EE1006_ALUControlUnit_main main_4 (.in_1(main_2_aluop), .in_2(im0_q[5:0]), .out_3(main_4_out_3));
  Shifter #(.width(32)) shifter_1 (.in(bit_extender_1_out), .\dist (5'b00010), .out(shifter_1_out));
  B23EE1006_ALUMain_main main_5 (
    .in_1(main_3_out_7), .in_2(multiplexer_2_out), .in_3(main_4_out_3), .Zero(main_5_zero), .out_5(out_2));  // open: out_6, out_7
  B23EE1006_ALUMain_main main_6 (
    .in_1(main_1_out_5), .in_2(shifter_1_out), .in_3(4'b0010), .out_5(main_6_out_5));  // open: Zero, out_6, out_7
  Multiplexer #(.width(32), .enable("false")) multiplexer_3 (
    .in0(main_1_out_5), .in1(main_6_out_5), .out(multiplexer_3_out), .sel(and_1_out));
  and and_1 (and_1_out, main_2_branch, main_5_zero, Clock_out);

  // Notes on the sheet:
  //   B23EE1006
endmodule
