// Logisim project B23EE1006_ALUMain.circ as structural Verilog: 1 circuit, main circuit main
module main (
  input  [31:0] in_1,
  input  [31:0] in_2,
  input  [3:0] in_3,
  output Zero,
  output [31:0] out_5,
  output out_6,
  output out_7
);

  wire or_2_out;
  wire [30:0] adder_1_out;
  wire [31:0] and_1_out, bit_extender_1_out, multiplexer_1_out, multiplexer_2_out, not_1_out, not_2_out,
       or_1_out;

  assign not_1_out = ~in_1;  // NOT_Gate not_1, 32 bits wide
  assign not_2_out = ~in_2;  // NOT_Gate not_2, 32 bits wide
  Multiplexer #(.width(32), .enable("false")) multiplexer_1 (
    .in0(in_1), .in1(not_1_out), .out(multiplexer_1_out), .sel(in_3[3]));
  Multiplexer #(.width(32), .enable("false")) multiplexer_2 (
    .in0(in_2), .in1(not_2_out), .out(multiplexer_2_out), .sel(in_3[2]));
  Adder #(.width(32)) adder_1 (
    .a(multiplexer_1_out), .b(multiplexer_2_out), .out({out_6, adder_1_out}), .cin(in_3[2]), .cout(out_7));
  assign and_1_out = multiplexer_1_out & multiplexer_2_out;  // AND_Gate and_1, 32 bits wide
  assign or_1_out = multiplexer_1_out | multiplexer_2_out;  // OR_Gate or_1, 32 bits wide
  assign bit_extender_1_out = {{31{1'b0}}, out_6};  // Bit_Extender bit_extender_1
  Multiplexer #(.select(2), .width(32), .enable("false")) multiplexer_3 (
    .in0(and_1_out), .in1(or_1_out), .in2({out_6, adder_1_out}), .in3(bit_extender_1_out), .out(out_5),
    .sel(in_3[1:0]));
  not not_3 (Zero, or_2_out);
  or or_2 (or_2_out, out_5[0], out_5[1], out_5[2], out_5[3], out_5[4], out_5[5], out_5[6], out_5[7], out_5[8], out_5[9], out_5[10], out_5[11], out_5[12], out_5[13], out_5[14], out_5[15], out_5[16], out_5[17], out_5[18], out_5[19], out_5[20], out_5[21], out_5[22], out_5[23], out_5[24], out_5[25], out_5[26], out_5[27], out_5[28], out_5[29], out_5[30], out_5[31]);

  // Notes on the sheet:
  //   A
  //   B
  //   ALU Control  
  //   Select line for A/~A
  //   Select line for B/~B
  //   Select line for Operation
  //    ALU Circuit 32-bit
  //   32-bit Zero Extension of MSB
  //   Overflow
  //   Carry Out
  //   ALU Result
endmodule
