// Logisim project ALUCtrlUnit.circ as structural Verilog: 1 circuit, main circuit main
module main (
  input  [1:0] in_1,
  input  [5:0] in_2,
  output [3:0] out_3
);

  wire and_2_out, not_1_out, not_2_out, or_1_out;

  and and_1 (out_3[0], in_1[1], or_1_out);
  or or_1 (or_1_out, in_2[0], in_2[3]);
  not not_1 (not_1_out, in_1[1]);
  or or_2 (out_3[1], not_1_out, not_2_out);
  not not_2 (not_2_out, in_2[2]);
  or or_3 (out_3[2], in_1[0], and_2_out);
  and and_2 (and_2_out, in_1[1], in_2[1]);

  assign out_3[3] = 1'b0;

  // Notes on the sheet:
  //   ALU Control Unit
  //   Funct
  //   (From Instruction Set)
  //   ALUop
  //   (From Main Control Unit)
  //   ALUControl
endmodule
