// Logisim project B23EE1006_CompleteProcessor.circ as structural Verilog: 1 circuit, main circuit main
module main (
);

  wire and_1_out, Clock_out, main_2_alusrc, main_2_branch, main_2_memread, main_2_memtoreg, main_2_memwrite,
       main_2_regdst, main_2_regwrite, main_4_zero;
  wire [1:0] main_2_aluop;
  wire [3:0] main_3_out_3;
  wire [4:0] multiplexer_1_out;
  wire [31:0] b23ee1006_data_mem_1_mem_output, b23ee1006_inst_mem_1_instruction_output,
       b23ee1006_pc_counter_1_pc_output, b23ee1006_reg_file_1_read_data1, b23ee1006_reg_file_1_read_data2,
       bit_extender_1_out, im0_q, im1_q, main_1_out_5, main_4_out_5, main_5_out_5, multiplexer_2_out,
       multiplexer_3_out, multiplexer_4_out, shifter_1_out;

  b23ee1006_pc_counter b23ee1006_pc_counter_1 (
    .pc_input(im1_q), .clock(Clock_out), .pc_output(b23ee1006_pc_counter_1_pc_output));
  Register #(.width(32)) im1 (.D(multiplexer_3_out), .Q(im1_q), .clk(Clock_out));  // open: en, clr
  Clock Clock (.out(Clock_out));
  b23ee1006_inst_mem b23ee1006_inst_mem_1 (
    .inst_input(b23ee1006_pc_counter_1_pc_output[23:0]),
    .instruction_output(b23ee1006_inst_mem_1_instruction_output));
  Register #(.width(32)) im0 (
    .D(b23ee1006_inst_mem_1_instruction_output), .Q(im0_q), .clk(Clock_out));  // open: en, clr
  ALU_main main_1 (
    .in_1(im1_q), .in_2(32'h4), .in_3(4'b0010), .out_5(main_1_out_5));  // open: Zero, Overflow, Carry_Out
  Multiplexer #(.width(5), .enable("false")) multiplexer_1 (
    .in0(im0_q[20:16]), .in1(im0_q[15:11]), .out(multiplexer_1_out), .sel(main_2_regdst));
  assign bit_extender_1_out = {{16{im0_q[15]}}, im0_q[15:0]};  // Bit_Extender bit_extender_1
  ControlUnit_main main_2 (
    .Opcode(im0_q[31:26]), .RegDst(main_2_regdst), .ALUSrc(main_2_alusrc), .MemToReg(main_2_memtoreg),
    .RegWrite(main_2_regwrite), .MemRead(main_2_memread), .MemWrite(main_2_memwrite), .Branch(main_2_branch),
    .ALUOp(main_2_aluop));
  b23ee1006_reg_file b23ee1006_reg_file_1 (
    .rd_input(multiplexer_4_out), .rw_enable(main_2_regwrite), .rd(multiplexer_1_out), .clock(Clock_out),
    .rt(im0_q[20:16]), .rs(im0_q[25:21]), .read_data2(b23ee1006_reg_file_1_read_data2),
    .read_data1(b23ee1006_reg_file_1_read_data1));
  Multiplexer #(.width(32), .enable("false")) multiplexer_2 (
    .in0(b23ee1006_reg_file_1_read_data2), .in1(bit_extender_1_out), .out(multiplexer_2_out),
    .sel(main_2_alusrc));
  ALUCtrlUnit_main main_3 (.in_1(main_2_aluop), .in_2(im0_q[5:0]), .out_3(main_3_out_3));
  Shifter #(.width(32)) shifter_1 (.in(bit_extender_1_out), .\dist (5'b00010), .out(shifter_1_out));
  ALU_main main_4 (
    .in_1(b23ee1006_reg_file_1_read_data1), .in_2(multiplexer_2_out), .in_3(main_3_out_3),
    .Zero(main_4_zero), .out_5(main_4_out_5));  // open: Overflow, Carry_Out
  ALU_main main_5 (
    .in_1(main_1_out_5), .in_2(shifter_1_out), .in_3(4'b0010), .out_5(main_5_out_5));  // open: Zero, Overflow, Carry_Out
  b23ee1006_data_mem b23ee1006_data_mem_1 (
    .mem_input(main_4_out_5), .data_input(b23ee1006_reg_file_1_read_data2), .mem_write(main_2_memwrite),
    .clock(Clock_out), .mem_read(main_2_memread), .mem_output(b23ee1006_data_mem_1_mem_output));
  Multiplexer #(.width(32), .enable("false")) multiplexer_3 (
    .in0(main_1_out_5), .in1(main_5_out_5), .out(multiplexer_3_out), .sel(and_1_out));
  and and_1 (and_1_out, main_2_branch, main_4_zero);
  Multiplexer #(.width(32), .enable("false")) multiplexer_4 (
    .in0(main_4_out_5), .in1(b23ee1006_data_mem_1_mem_output), .out(multiplexer_4_out), .sel(main_2_memtoreg));

  // Notes on the sheet:
  //   B23EE1006
  //   CIRCUIT
endmodule
